# Fritzing sketch practica3 (saved by Fritzing 0.9.3b)
breadboards: 2

parts:
  LED1 = smd LED [color="Red (633nm)" package="1206 [SMD]"]
  R4 = Resistor [tolerance=±5% resistance=4.7k package="0805 [SMD]"]
  J4 = male pin header, 4 pins [form="♂ (male)"]
  J5 = male pin header, 3 pins [form="♂ (male)"]
  Sensor_PIR_HC-SR503 = HC-SR501 Body Sensor Module
  U2 = GAS_SENSOR [part_number=MQ2 package=mq-3]  # not connected
  Componente6 = Arduino Nano (Rev3.0)
  R5 = Resistor [tolerance=±5% resistance=330 package="0805 [SMD]"]
  Q2 = LTR-301 [package=ltr-301]
  R6 = Resistor [tolerance=±5% resistance=10k package="0805 [SMD]"]
  R7 = Resistor [tolerance=±5% resistance=1k package="0805 [SMD]"]
  R8 = Resistor [tolerance=±5% resistance=10k package="0805 [SMD]"]
  Q3 = TRANSISTOR_NPN [package=to-92]
  RS232 = Camdenboss CTB0158-5 [part_number=RS232 package=THT]

nets (from the schematic view):
  N1: LED1.cathode, R5.Pin_1
  GND: LED1.anode, J4.pin2, J5.pin1, Sensor_PIR_HC-SR503.GND, Componente6.GND
  N2: R4.Pin_0, J5.pin2, Sensor_PIR_HC-SR503.OUT, Componente6.D3, Componente6.D4
  VCC: R4.Pin_1, J4.pin1, J5.pin3, Sensor_PIR_HC-SR503.VCC, Componente6.5V
  N3: J4.pin4, Componente6.A0
  N4: Componente6.D1/TX, R5.Pin_0
  N5: Q2.C, R6.Pin_0, R7.Pin_0
  N6: Q2.E, Q3.E, RS232.pin1
  N7: R6.Pin_1, R8.Pin_0, RS232.pin4
  N8: R7.Pin_1, Q3.B
  N9: R8.Pin_1, Q3.C, RS232.pin2

notes:
  RS232
  -3.4vcc
  -5vcc
  -TXD
  -RXD
  -GND

custom parts:
  HC-SR501 Body Sensor Module: Pyroelectric Infrared PIR Motion Sensor Detector Module
